# Fritzing sketch force (saved by Fritzing 0.9.3b)
breadboards: 2

parts:
  U1 = NodeMCU V1.0
  J1 = Basic Force Sensing Resistor (FSR) [package=THT]
  R1 = Resistor [tolerance=±5% resistance=220 package=THT]
  R2 = Resistor [tolerance=±5% resistance=220 package=THT]
  R3 = Resistor [tolerance=±5% resistance=220 package=THT]

nets:
  N1: U1.3V3, R2.Pin_0
  N2: U1.GND, J1.pin_1
  N3: U1.A0, J1.pin_0, R1.Pin_1
  N4: R1.Pin_0, R3.Pin_1
  N5: R2.Pin_1, R3.Pin_0

custom parts:
  NodeMCU V1.0: ESP8266 based NodeMCU
