# Fritzing sketch led (saved by Fritzing 0.9.3b)
breadboards: 2

parts:
  U1 = NodeMCU V1.0
  LED3 = RGB LED (com. cathode, rbg) [package="5 mm [THT]"]
  R1 = Resistor [tolerance=±5% resistance=220 package="0402 [SMD]"]
  R2 = Resistor [tolerance=±5% resistance=220 package="0402 [SMD]"]
  R3 = Resistor [tolerance=±5% resistance=220 package="0402 [SMD]"]

nets:
  N1: U1.D1, R1.Pin_0
  N2: U1.GND, LED3.common_cathode
  N3: U1.D5, R2.Pin_0
  N4: U1.D6, R3.Pin_0
  N5: LED3.red_anode, R1.Pin_1
  N6: LED3.blue_anode, R2.Pin_1
  N7: LED3.green_anode, R3.Pin_1

custom parts:
  NodeMCU V1.0: ESP8266 based NodeMCU
